# Fritzing sketch pori (saved by Fritzing 0.9.3b)
breadboards: 1

parts:
  パーツ1 = Arduino Uno (Rev3) - ICSP
  パーツ2 = LCD1602-I2C
  R1 = Trimmer Potentiometer [maximum_resistance=10kΩ package=THT]
  U1 = GP-2106 [package=gp-2106]  # not connected
  J1 = Basic Servo
  J3 = Infrared Proximity Sensor

nets:
  N1: パーツ1.A3, J3.Vout
  VCC: パーツ1.5V, パーツ2.VCC, R1.leg2, J1.vcc, J3.Vcc
  N2: パーツ1.D3_PWM, J1.pulse
  GND: パーツ1.GND, パーツ2.GND, R1.leg1, J1.gnd, J3.GND

custom parts:
  LCD1602-I2C: A standard character display, usually with 2x16 characters. Comes in many colors with LCM1602 IIC attached.
